# Fritzing sketch Ardusajzer v01 (saved by Fritzing 0.9.3b)
circuit board: 17.374cm x 13.8944cm
breadboards: 4

parts:
  Part1 = Arduino Uno (Rev3)
  R2 = Resistor [tolerance=±5% resistance=220 package=THT]
  R3 = Resistor [tolerance=±5% resistance=220 package=THT]
  S4 = Momentary Switch [package=ksa_sealed_tac_switch]
  S5 = Momentary Switch [package=ksa_sealed_tac_switch]
  S6 = Momentary Switch [package=ksa_sealed_tac_switch]
  LED1 = smd LED [color="Red (633nm)" package="0805 [SMD]"]
  S10 = Pushbutton [package="[SMD]"]
  S11 = Pushbutton [package="[THT]"]
  R4 = Resistor [tolerance=±5% resistance=220 package="2010 [SMD]"]
  S12 = Momentary Switch [package=ksa_sealed_tac_switch]
  S13 = Momentary Switch [package=ksa_sealed_tac_switch]
  S14 = Momentary Switch [package=ksa_sealed_tac_switch]
  S15 = Momentary Switch [package=ksa_sealed_tac_switch]
  S16 = Momentary Switch [package=ksa_sealed_tac_switch]
  S17 = Momentary Switch [package=ksa_sealed_tac_switch]
  S18 = Momentary Switch [package=ksa_sealed_tac_switch]
  S19 = Momentary Switch [package=ksa_sealed_tac_switch]
  U3 = POT [package=pot_alpha_rv16af-20]
  U4 = POT [package=pot_alpha_rv16af-20]
  J1 = Piezo Speaker
  R5 = Resistor [tolerance=±5% resistance=220 package="2010 [SMD]"]
  U2 = POT [package=pot_alpha_rv16af-20]
  U5 = LCD-16X2 [package=lcd-8x2-kit]
  U6 = 74HC595 [package="DIP16 [THT]"]
  LED2 = LED - 5mm [color="Red (633nm)" package="5 mm [THT]"]
  LED3 = LED - 5mm [color="Red (633nm)" package="5 mm [THT]"]
  LED4 = LED - 5mm [color="Red (633nm)" package="5 mm [THT]"]
  LED5 = LED - 5mm [color="Red (633nm)" package="5 mm [THT]"]
  LED6 = LED - 5mm [color="Red (633nm)" package="5 mm [THT]"]
  LED7 = LED - 5mm [color="Red (633nm)" package="5 mm [THT]"]
  LED8 = LED - 5mm [color="Red (633nm)" package="5 mm [THT]"]
  LED9 = LED - 5mm [color="Red (633nm)" package="5 mm [THT]"]
  Part2 = Arduino Uno (Rev3)
  R6 = Resistor [tolerance=±5% resistance=220 package=THT]
  R7 = Resistor [tolerance=±5% resistance=220 package=THT]
  R8 = Resistor [tolerance=±5% resistance=220 package=THT]
  R9 = Resistor [tolerance=±5% resistance=220 package=THT]
  R10 = Resistor [tolerance=±5% resistance=220 package=THT]
  R11 = Resistor [tolerance=±5% resistance=220 package=THT]
  R12 = Resistor [tolerance=±5% resistance=220 package=THT]
  R13 = Resistor [tolerance=±5% resistance=220 package=THT]

nets (from the breadboard view):
  GND: Part1.A3, Part1.GND, S4.3, S5.3, S6.3, LED1.cathode, S10.Pin_3, S10.Pin_4, S11.Pin_3, S11.Pin_4, S12.4, S13.4, S14.4, S15.4, S16.4, S17.4, S18.4, S19.4, U3.E, U4.E, R5.Pin_0, U2.S, U5.DB7, U5.K, U6.GND, Part2.GND
  N1: Part1.A4/SDA, R3.Pin_1, Part2.A4/SDA
  N2: Part1.A5/SCL, R2.Pin_1, Part2.A5/SCL
  N3: Part1.D8, U5.DB3
  N4: Part1.D9_PWM, U5.DB1
  N5: Part1.D10_PWM/SS, U5.E
  N6: Part1.D11_PWM/MOSI, U5.RS
  N7: Part1.D12/MISO, U5.VDD
  N8: Part1.D13/SCK, R4.Pin_1
  N9: Part1.D2, S6.2
  N10: Part1.D3_PWM, S5.2
  N11: Part1.D4, S11.Pin_1, S11.Pin_2
  N12: Part1.D5_PWM, S4.2
  5V: Part1.5V, R2.Pin_0, R3.Pin_0, U3.A, U4.A, U2.E, U5.DB5, U6.VCC, Part2.5V
  N13: LED1.anode, R4.Pin_0
  N14: S10.Pin_1, S10.Pin_2, Part2.D0/RX
  N15: S12.1, Part2.D2
  N16: S13.1, Part2.D3_PWM
  N17: S14.1, Part2.D4
  N18: S15.1, Part2.D5_PWM
  N19: S16.1, Part2.D6_PWM
  N20: S17.1, Part2.D7
  N21: S18.1, Part2.D8
  N22: S19.1, Part2.D9_PWM
  N23: U3.S, Part2.A3
  N24: U4.S, Part2.A2
  N25: J1.pin1, R5.Pin_1
  N26: J1.pin2, Part2.D10_PWM/SS
  N27: U6.Q1, R7.Pin_1
  N28: U6.Q2, R8.Pin_1
  N29: U6.Q3, R9.Pin_1
  N30: U6.Q4, R10.Pin_1
  N31: U6.Q5, R11.Pin_1
  N32: U6.Q6, R12.Pin_1
  N33: U6.Q7, R13.Pin_1
  N34: U6.SH_CP, Part2.D13/SCK
  N35: U6.ST_CP, Part2.D12/MISO
  N36: U6.DS, Part2.D11_PWM/MOSI
  N37: U6.Q0, R6.Pin_1
  N38: LED2.anode, R6.Pin_0
  N39: LED3.anode, R7.Pin_0
  N40: LED4.anode, R8.Pin_0
  N41: LED5.anode, R9.Pin_0
  N42: LED6.anode, R10.Pin_0
  N43: LED7.anode, R11.Pin_0
  N44: LED8.anode, R12.Pin_0
  N45: LED9.anode, R13.Pin_0
